// Logisim project ALU.circ as structural Verilog: 4 circuits, main circuit main
module main (
  input  [2:0] mode,
  input  SELA,
  input  SELB,
  input  SELO,
  input  [15:0] DBUS,
  output FL_S,
  output FL_Z,
  output FL_N,
  output FL_V,
  output FL_C,
  output [15:0] DBUS_OUT
);

  wire demultiplexer_1_out0, demultiplexer_1_out1, demultiplexer_1_out2, demultiplexer_1_out3,
       demultiplexer_1_out4, not_1_out;
  wire [15:0] alu_compute_result_1_alu_compute_result, register_1_q, register_2_q;

  Register #(.trigger("falling"), .width(16)) register_1 (
    .D(DBUS), .en(1'b1), .clk(SELA), .Q(register_1_q));  // open: clr
  Register #(.trigger("falling"), .width(16)) register_2 (
    .D(DBUS), .en(1'b1), .clk(SELB), .Q(register_2_q));  // open: clr
  Demultiplexer #(.select(3)) demultiplexer_1 (
    .out0(demultiplexer_1_out0), .out1(demultiplexer_1_out1), .out2(demultiplexer_1_out2),
    .out3(demultiplexer_1_out3), .out4(demultiplexer_1_out4), .in(1'b1), .sel(mode));  // open: out5, out6, out7
  ALU_compute_result alu_compute_result_1 (
    .IN_A(register_1_q), .EN_AND(demultiplexer_1_out0), .IN_B(register_2_q), .EN_OR(demultiplexer_1_out1),
    .EN_ADD(demultiplexer_1_out2), .EN_SUB(demultiplexer_1_out3), .EN_XOR(demultiplexer_1_out4),
    .ALU_COMPUTE_RESULT(alu_compute_result_1_alu_compute_result));
  not not_1 (not_1_out, SELO);
  assign DBUS_OUT = not_1_out ? alu_compute_result_1_alu_compute_result : 16'bz;  // Controlled_Buffer controlled_buffer_1
  ALU_flag_compute alu_flag_compute_1 (
    .Result_pin(alu_compute_result_1_alu_compute_result), .AND_NOTE(demultiplexer_1_out0),
    .OR_NOTE(demultiplexer_1_out1), .XOR_NOTE(demultiplexer_1_out4), .A15(register_1_q[15]),
    .B15(register_2_q[15]), .ADD_NOTE(demultiplexer_1_out2), .SUB_NOTE(demultiplexer_1_out3), .FL_S(FL_S),
    .FL_Z(FL_Z), .FL_N(FL_N), .FL_V(FL_V), .FL_C(FL_C));
  _74244 u_74244_1 ();  // open: pin1, pin2, pin3, pin4, pin5, pin6, pin7, pin8, pin9, pin19, pin18, pin17, pin16, pin15, pin14, pin13, pin12, pin11
  _74244 u_74244_2 ();  // open: pin1, pin2, pin3, pin4, pin5, pin6, pin7, pin8, pin9, pin19, pin18, pin17, pin16, pin15, pin14, pin13, pin12, pin11

  // Notes on the sheet:
  //   INPUT A LATCH
  //   TRISTATE BUFFER
endmodule

module ALU_compute_result (
  input  [15:0] IN_A,
  input  EN_AND,
  input  [15:0] IN_B,
  input  EN_OR,
  input  EN_ADD,
  input  EN_SUB,
  input  EN_XOR,
  output [15:0] ALU_COMPUTE_RESULT
);

  wire [15:0] adder_1_out, AND_GATE_out, OR_GATE_out, subtractor_1_out, xor_1_out;

  assign AND_GATE_out = IN_A & IN_B;  // AND_Gate AND_GATE, 16 bits wide
  assign OR_GATE_out = IN_A | IN_B;  // OR_Gate OR_GATE, 16 bits wide
  Adder #(.width(16)) adder_1 (.a(IN_A), .b(IN_B), .out(adder_1_out));  // open: cin, cout
  Subtractor #(.width(16)) subtractor_1 (.a(IN_A), .b(IN_B), .out(subtractor_1_out));  // open: bin, bout
  assign xor_1_out = IN_A ^ IN_B;  // XOR_Gate xor_1, 16 bits wide
  assign ALU_COMPUTE_RESULT = EN_AND ? AND_GATE_out : 16'bz;  // Controlled_Buffer AND_BUFFER
  assign ALU_COMPUTE_RESULT = EN_OR ? OR_GATE_out : 16'bz;  // Controlled_Buffer OR_BUFFER
  assign ALU_COMPUTE_RESULT = EN_ADD ? adder_1_out : 16'bz;  // Controlled_Buffer ADD_BUFFER
  assign ALU_COMPUTE_RESULT = EN_SUB ? subtractor_1_out : 16'bz;  // Controlled_Buffer SUB_BUFFER
  assign ALU_COMPUTE_RESULT = EN_XOR ? xor_1_out : 16'bz;  // Controlled_Buffer XOR_BUFFER
endmodule

module ALU_flag_compute (
  input  [15:0] Result_pin,
  input  AND_NOTE,
  input  OR_NOTE,
  input  XOR_NOTE,
  input  A15,
  input  B15,
  input  ADD_NOTE,
  input  SUB_NOTE,
  output FL_S,
  output FL_Z,
  output FL_N,
  output FL_V,
  output FL_C
);

  wire and_1_out, and_2_out, and_3_out, and_4_out, and_5_out, and_6_out, and_7_out, and_8_out, and_9_out,
       and_10_out, buffer_1_out, buffer_2_out, buffer_3_out, buffer_4_out, buffer_5_out, buffer_6_out,
       buffer_7_out, buffer_8_out, buffer_9_out, buffer_10_out, multiplexer_2_out, or_1_out, or_2_out,
       or_3_out, or_4_out, or_5_out;

  or or_1 (or_1_out, AND_NOTE, OR_NOTE, XOR_NOTE);
  buf buffer_1 (buffer_1_out, A15);
  buf buffer_2 (buffer_2_out, B15);
  buf buffer_3 (buffer_3_out, Result_pin[15]);
  buf buffer_4 (buffer_4_out, Result_pin[15]);
  buf buffer_5 (buffer_5_out, B15);
  buf buffer_6 (buffer_6_out, A15);
  buf buffer_7 (buffer_7_out, Result_pin[15]);
  buf buffer_8 (buffer_8_out, Result_pin[15]);
  buf buffer_9 (buffer_9_out, A15);
  buf buffer_10 (buffer_10_out, A15);
  xor xor_1 (FL_S, Result_pin[15], FL_V);
  and and_1 (and_1_out, Result_pin[15], buffer_1_out, buffer_2_out);
  and and_2 (and_2_out, buffer_3_out, A15, B15);
  and and_3 (and_3_out, buffer_4_out, A15, buffer_5_out);
  and and_4 (and_4_out, Result_pin[15], buffer_6_out, B15);
  and and_5 (and_5_out, A15, B15);
  and and_6 (and_6_out, B15, buffer_7_out);
  and and_7 (and_7_out, A15, buffer_8_out);
  and and_8 (and_8_out, buffer_9_out, B15);
  and and_9 (and_9_out, B15, Result_pin[15]);
  and and_10 (and_10_out, buffer_10_out, Result_pin[15]);
  nor nor_1 (FL_Z, Result_pin[0], Result_pin[1], Result_pin[2], Result_pin[3], Result_pin[4], Result_pin[5], Result_pin[6], Result_pin[7], Result_pin[8], Result_pin[9], Result_pin[10], Result_pin[11], Result_pin[12], Result_pin[13], Result_pin[14], Result_pin[15]);
  or or_2 (or_2_out, and_1_out, and_2_out);
  or or_3 (or_3_out, and_3_out, and_4_out);
  or or_4 (or_4_out, and_5_out, and_6_out, and_7_out);
  or or_5 (or_5_out, and_8_out, and_9_out, and_10_out);
  Multiplexer multiplexer_1 (.in0(multiplexer_2_out), .in1(1'b0), .out(FL_V), .sel(or_1_out));
  Multiplexer multiplexer_2 (.in0(or_2_out), .in1(or_3_out), .out(multiplexer_2_out), .sel(ADD_NOTE));
  Multiplexer multiplexer_3 (.in0(or_4_out), .in1(or_5_out), .out(FL_C), .sel(SUB_NOTE));

  assign FL_N = Result_pin[15];
endmodule

module Latch (
  input  S,
  input  R,
  output Q,
  output NotQ
);

  wire not_1_out, not_2_out;

  not not_1 (not_1_out, S);
  not not_2 (not_2_out, R);
  nand nand_1 (Q, not_1_out, NotQ);
  nand nand_2 (NotQ, Q, not_2_out);
endmodule
