// Logisim project ALU_flag_blcok.circ as structural Verilog: 1 circuit, main circuit main
module main (
  input  FL_N,
  input  FL_V,
  input  [15:0] in_3,
  input  in_4,
  input  AND_NOTE,
  input  OR_NOTE,
  input  XOR_NOTE,
  input  R15,
  input  A15,
  input  B15,
  output FL_S,
  output FL_Z,
  output FL_N_NOTE,
  output FL_V_NOTE
);

  wire and_1_out, and_2_out, and_3_out, and_4_out, buffer_1_out, buffer_2_out, buffer_3_out, buffer_4_out,
       buffer_5_out, buffer_6_out;

  or or_1 (FL_V_NOTE, AND_NOTE, OR_NOTE, XOR_NOTE);
  buf buffer_1 (buffer_1_out, A15);
  buf buffer_2 (buffer_2_out, B15);
  buf buffer_3 (buffer_3_out, R15);
  buf buffer_4 (buffer_4_out, R15);
  buf buffer_5 (buffer_5_out, B15);
  buf buffer_6 (buffer_6_out, A15);
  xor xor_1 (FL_S, FL_N, FL_V);
  and and_1 (and_1_out, R15, buffer_1_out, buffer_2_out);
  and and_2 (and_2_out, buffer_3_out, A15, B15);
  and and_3 (and_3_out, buffer_4_out, A15, buffer_5_out);
  and and_4 (and_4_out, R15, buffer_6_out, B15);
  nand nand_1 (FL_Z, in_3[0], in_3[1], in_3[2], in_3[3], in_3[4], in_3[5], in_3[6], in_3[7], in_3[8], in_3[9], in_3[10], in_3[11], in_3[12], in_3[13], in_3[14], in_3[15]);
  or or_2 (FL_V_NOTE, and_1_out, and_2_out);
  or or_3 (FL_V_NOTE, and_3_out, and_4_out);

  assign FL_N_NOTE = in_4;
endmodule
