// Logisim project Matsuzaka_I_computer.circ as structural Verilog: 3 circuits, main circuit Matsuzaka_ALU
module Matsuzaka_ALU (
  input  [15:0] INPUT_A,
  input  ZERO_A,
  input  NEGATE_A,
  input  [15:0] INPUT_B,
  input  [2:0] SELECT_MODE,
  input  ZERO_OUT,
  input  NEGATE_OUT,
  input  ZERO_B,
  input  NEGATE_B,
  output [15:0] out_10
);

  wire [15:0] ADD_OUT, AND_OUT, INA, INB, multiplexer_1_out, multiplexer_2_out, multiplexer_5_out,
       multiplexer_6_out, not_1_out, not_2_out, not_3_out, OR_OUT, SUB_OUT, XOR_OUT;

  Multiplexer #(.width(16)) multiplexer_1 (.in0(INPUT_A), .in1({16{1'b0}}), .out(multiplexer_1_out), .sel(ZERO_A));
  Multiplexer #(.width(16)) multiplexer_2 (.in0(INPUT_B), .in1({16{1'b0}}), .out(multiplexer_2_out), .sel(ZERO_B));
  assign not_1_out = ~multiplexer_1_out;  // NOT_Gate not_1, 16 bits wide
  assign not_2_out = ~multiplexer_2_out;  // NOT_Gate not_2, 16 bits wide
  Multiplexer #(.width(16)) multiplexer_3 (.in0(multiplexer_1_out), .in1(not_1_out), .out(INA), .sel(NEGATE_A));
  Multiplexer #(.width(16)) multiplexer_4 (.in0(multiplexer_2_out), .in1(not_2_out), .out(INB), .sel(NEGATE_B));
  assign AND_OUT = INA & INB;  // AND_Gate and_1, 16 bits wide
  assign OR_OUT = INA | INB;  // OR_Gate or_1, 16 bits wide
  assign XOR_OUT = INA ^ INB;  // XOR_Gate xor_1, 16 bits wide
  Adder #(.width(16)) adder_1 (.a(INA), .b(INB), .out(ADD_OUT));  // open: cin, cout
  Subtractor #(.width(16)) subtractor_1 (.a(INA), .b(INB), .out(SUB_OUT));  // open: bin, bout
  Multiplexer #(.select(3), .width(16)) multiplexer_5 (
    .in0(AND_OUT), .in1(OR_OUT), .in2(XOR_OUT), .in3(ADD_OUT), .in4(SUB_OUT), .out(multiplexer_5_out),
    .sel(SELECT_MODE));  // open: in5, in6, in7
  Multiplexer #(.width(16)) multiplexer_6 (
    .in0(multiplexer_5_out), .in1({16{1'b0}}), .out(multiplexer_6_out), .sel(ZERO_OUT));
  assign not_3_out = ~multiplexer_6_out;  // NOT_Gate not_3, 16 bits wide
  Multiplexer #(.width(16)) multiplexer_7 (.in0(multiplexer_6_out), .in1(not_3_out), .out(out_10), .sel(NEGATE_OUT));

  // Notes on the sheet:
  //   INPUT_A
  //   INPUT_B
  //   AND
  //   OR
  //   XOR
  //   ADD
endmodule

module Matsuzaka_CPU (
  input  [15:0] in_1,
  input  in_2,
  input  [15:0] in_3,
  input  in_4,
  input  in_5,
  input  [15:0] in_6,
  input  in_7,
  input  in_8,
  input  [1:0] in_9,
  input  in_10,
  input  in_11,
  input  [15:0] in_12,
  output [15:0] out_13
);

  wire clock_1_out;
  wire [2:2] undriven;
  wire [15:0] Data_memory_data, Instruction_memory_data, multiplexer_1_out;

  ROM #(.addrWidth(16), .dataWidth(16)) Instruction_memory (.addr(in_1), .data(Instruction_memory_data));
  ROM #(.addrWidth(16), .dataWidth(16)) Data_memory (.addr(in_12), .data(Data_memory_data));
  Multiplexer #(.width(16)) multiplexer_1 (
    .in0(Instruction_memory_data), .in1(Data_memory_data), .out(multiplexer_1_out), .sel(in_2));
  Clock clock_1 (.out(clock_1_out));
  Register #(.width(16)) register_1 (.D(multiplexer_1_out), .en(1'b1), .clk(clock_1_out));  // open: Q, clr
  Matsuzaka_ALU matsuzaka_alu_1 (
    .ZERO_B(in_7), .NEGATE_B(in_8), .ZERO_A(in_4), .NEGATE_A(in_5), .INPUT_B(in_6), .INPUT_A(in_3),
    .SELECT_MODE({undriven[2], in_9}), .ZERO_OUT(in_10), .NEGATE_OUT(in_11), .out_10(out_13));
  // Pins of 2 and 3 bits meet at {undriven[2], in_9}

  // Notes on the sheet:
  //   contents of Instruction_memory (hex, n*v repeats v):
  //   1233 4426 ff25 551a 4112 41 599 559
endmodule

module Control_unit (
  input  [1:0] Function_group,
  input  Reg_amount,
  input  No_register,
  input  [3:0] Specific_function
);
endmodule
